# Fritzing sketch l298n-arduino (saved by Fritzing 0.9.10b)

parts:
  부품1 = Arduino Mega 2560 (Rev3)
  S1 = H-Bridge with L298N
  VCC1 = Battery

nets:
  5V: 부품1.5V, S1.5V
  GND: 부품1.GND, S1.GND, VCC1.-
  N1: S1.12V, VCC1.+

custom parts:
  H-Bridge with L298N: h-bridge
