# Fritzing sketch l298n-arduino_motor (saved by Fritzing 0.9.10b)

parts:
  부품1 = Arduino Mega 2560 (Rev3)
  S1 = H-Bridge with L298N
  VCC1 = Battery

nets:
  N1: 부품1.D13_PWM, S1.ENB
  N2: 부품1.D12_PWM, S1.IN4
  N3: 부품1.D11_PWM, S1.IN3
  N4: 부품1.D10_PWM, S1.IN2
  N5: 부품1.D9_PWM, S1.IN1
  N6: 부품1.D8_PWM, S1.ENA
  5V: 부품1.5V, S1.5V
  GND: 부품1.GND, S1.GND, VCC1.-
  N7: S1.12V, VCC1.+

custom parts:
  H-Bridge with L298N: h-bridge
